# Fritzing sketch arduino_range_meter_and_display (saved by Fritzing 0.8.7b)
circuit board: 6.88566cm x 5.36311cm
breadboards: 1

parts:
  Part1 = Arduino Uno (Rev3)
  SONAR1 = Maxbotix MaxSonar Ultrasonic Sensor
  4Digit_7SEG2 = Sparkfun 4-digit 7-segment LED Display

nets:
  N1: Part1.D10_PWM/SS, 4Digit_7SEG2.CSN
  N2: Part1.D11_PWM/MOSI, 4Digit_7SEG2.SI
  N3: Part1.D13/SCK, 4Digit_7SEG2.SCK
  GND: Part1.GND, SONAR1.GND, 4Digit_7SEG2.GND
  N4: Part1.D3_PWM, SONAR1.PW
  5V: Part1.5V, SONAR1.+5V, 4Digit_7SEG2.VCC

custom parts:
  Maxbotix MaxSonar Ultrasonic Sensor: Maxbotix MaxSonar Ultrasonic Sensor LV-EZ0, LV-EZ1, LV-EZ2, LV-EZ3, LV-EZ4
  Sparkfun 4-digit 7-segment LED Display: 4-digit, 7-segment LED Display with SPI/Serial Control
